// Logisim project processor2.circ as structural Verilog: 8 circuits, main circuit main
module main (
);

  wire alu_1_zero, ALUSrc, and_1_out, Branch, button_1_out, clock, MemToReg, MemWrite, RegWrite;
  wire [1:0] ImmGen;
  wire [3:0] ALUControl, Func;
  wire [4:0] rom_1_data, rom_1_data_2, rom_1_data_3;
  wire [6:0] OpCode;
  wire [7:0] adder_1_out, multiplexer_1_out, PC_q;
  wire [31:0] adder_2_out, alu_1_result, bit_extender_1_out, data_mem_1_rd, immgen_1_out_3,
       multiplexer_2_out, multiplexer_3_out, register_1_read_data_1, register_1_read_data_2, shifter_1_out;
  wire [31:25] rom_1_data_4;

  Multiplexer #(.width(8), .enable("false")) multiplexer_1 (
    .in0(adder_1_out), .in1(adder_2_out[7:0]), .out(multiplexer_1_out), .sel(and_1_out));
  Clock clock_1 (.out(clock));
  Button button_1 (.out(button_1_out));
  Register PC (.D(multiplexer_1_out), .Q(PC_q), .clk(clock), .clr(button_1_out));  // open: en
  Subtractor subtractor_1 ();  // open: a, b, out, bin, bout
  CONTROL_UNIT control_unit_1 (
    .OPCode(OpCode), .Func(Func), .RegWrite(RegWrite), .ImmGen(ImmGen), .ALUSrc(ALUSrc), .Branch(Branch),
    .MemWrite(MemWrite), .MemToReg(MemToReg), .ALUControl(ALUControl));
  Adder adder_1 (.a(PC_q), .b(8'h4), .out(adder_1_out));  // open: cin, cout
  ROM #(.dataWidth(32)) rom_1 (
    .addr(PC_q),
    .data({rom_1_data_4[31], Func[3], rom_1_data_4[29:25], rom_1_data_3, rom_1_data_2, Func[2:0], rom_1_data, OpCode}));  // open: sel
  // Probe on rom_1_data_3
  // Probe on rom_1_data
  assign bit_extender_1_out = {{24{1'b0}}, PC_q};  // Bit_Extender bit_extender_1
  // Probe on rom_1_data_2
  ImmGen immgen_1 (
    .ImmSrc(ImmGen),
    .Inst({rom_1_data_4[31], Func[3], rom_1_data_4[29:25], rom_1_data_3, rom_1_data_2, Func[2:0], rom_1_data, OpCode}),
    .out_3(immgen_1_out_3));
  // Probe on register_1_read_data_1
  register register_1 (
    .Write_Data(multiplexer_3_out), .WE(RegWrite), .Write_Register_rd(rom_1_data), .Clock(clock),
    .Read_Data_1(register_1_read_data_1), .Read_Register_1_rs1(rom_1_data_2),
    .Read_Data_2(register_1_read_data_2), .Read_Register_2__rs2(rom_1_data_3));
  Multiplexer #(.width(32), .enable("false")) multiplexer_2 (
    .in0(register_1_read_data_2), .in1(immgen_1_out_3), .out(multiplexer_2_out), .sel(ALUSrc));
  Shifter #(.width(32)) shifter_1 (.in(immgen_1_out_3), .\dist (5'b00001), .out(shifter_1_out));
  ALU alu_1 (
    .Zero(alu_1_zero), .A(register_1_read_data_1), .Result(alu_1_result), .B(multiplexer_2_out),
    .ALUSel(ALUControl));  // open: Overflow
  Adder #(.width(32)) adder_2 (.a(shifter_1_out), .b(bit_extender_1_out), .out(adder_2_out));  // open: cin, cout
  // Probe on multiplexer_2_out
  and and_1 (and_1_out, Branch, alu_1_zero);
  data_mem data_mem_1 (
    .A(alu_1_result[8:0]), .CLK(clock), .WE(MemWrite), .WD(register_1_read_data_2), .RD(data_mem_1_rd));
  // Probe on MemToReg
  Multiplexer #(.width(32), .enable("false")) multiplexer_3 (
    .in0(alu_1_result), .in1(data_mem_1_rd), .out(multiplexer_3_out), .sel(MemToReg));
  // Probe on multiplexer_3_out

  // Notes on the sheet:
  //   contents of rom_1 (hex, n*v repeats v):
  //   0 2083 2083 2083 208093 108093 108093 108093 110113 210113 210113 210113 2090b3 2081b3 2081b3 2081b3
  //   1122b3 302423 302423 302423 113333 802203 802203 802203 143b3 420213 420213 420213 70d0b3 100b3
  //   138392 100b3 3e3b3 100b3 100b3 100b3 3f3b3 1000b3 7*81b3
endmodule

// Reg File
module register (
  input  [31:0] Write_Data,
  input  WE,
  input  [4:0] Read_Register_1_rs1,
  input  [4:0] Write_Register_rd,
  input  Clock,
  input  [4:0] Read_Register_2__rs2,
  output [31:0] Read_Data_1,
  output [31:0] Read_Data_2
);

  wire demultiplexer_1_out0, demultiplexer_1_out1, demultiplexer_1_out2, demultiplexer_1_out5,
       demultiplexer_1_out6, demultiplexer_1_out7, demultiplexer_1_out8, demultiplexer_1_out9,
       demultiplexer_1_out10;
  wire [31:0] x0__zero_q, x1__ra_q, x2__sp_q, x5__t0_q, x6__t1_q, x7__t2_q, x8__s0_q, x9__s1_q, x10__a0_q;

  Demultiplexer #(.select(5)) demultiplexer_1 (
    .out0(demultiplexer_1_out0), .out1(demultiplexer_1_out1), .out2(demultiplexer_1_out2),
    .out5(demultiplexer_1_out5), .out6(demultiplexer_1_out6), .out7(demultiplexer_1_out7),
    .out8(demultiplexer_1_out8), .out9(demultiplexer_1_out9), .out10(demultiplexer_1_out10), .in(WE),
    .sel(Write_Register_rd));  // open: out3, out4, out11, out12, out13, out14, out15, out16, out17, out18, out19, out20, out21, out22, out23, out24, out25, out26, out27, out28, out29, out30, out31, en
  Register #(.width(32)) x0__zero (
    .D({32{1'b0}}), .en(demultiplexer_1_out0), .Q(x0__zero_q), .clk(Clock));  // open: clr
  Register #(.width(32)) x1__ra (.D(Write_Data), .en(demultiplexer_1_out1), .Q(x1__ra_q), .clk(Clock));  // open: clr
  Register #(.width(32)) x2__sp (.D(Write_Data), .en(demultiplexer_1_out2), .Q(x2__sp_q), .clk(Clock));  // open: clr
  Register #(.width(32)) x5__t0 (.D(Write_Data), .en(demultiplexer_1_out5), .Q(x5__t0_q), .clk(Clock));  // open: clr
  Register #(.width(32)) x6__t1 (.D(Write_Data), .en(demultiplexer_1_out6), .Q(x6__t1_q), .clk(Clock));  // open: clr
  Register #(.width(32)) x7__t2 (.D(Write_Data), .en(demultiplexer_1_out7), .Q(x7__t2_q), .clk(Clock));  // open: clr
  Register #(.width(32)) x8__s0 (.D(Write_Data), .en(demultiplexer_1_out8), .Q(x8__s0_q), .clk(Clock));  // open: clr
  Register #(.width(32)) x9__s1 (.D(Write_Data), .en(demultiplexer_1_out9), .Q(x9__s1_q), .clk(Clock));  // open: clr
  Register #(.width(32)) x10__a0 (.D(Write_Data), .en(demultiplexer_1_out10), .Q(x10__a0_q), .clk(Clock));  // open: clr
  Multiplexer #(.select(5), .width(32)) multiplexer_1 (
    .in0(x0__zero_q), .in1(x1__ra_q), .in2(x2__sp_q), .in5(x5__t0_q), .in6(x6__t1_q), .in7(x7__t2_q),
    .in8(x8__s0_q), .in9(x9__s1_q), .in10(x10__a0_q), .out(Read_Data_1), .sel(Read_Register_1_rs1));  // open: in3, in4, in11, in12, in13, in14, in15, in16, in17, in18, in19, in20, in21, in22, in23, in24, in25, in26, in27, in28, in29, in30, in31, en
  Multiplexer #(.select(5), .width(32)) multiplexer_2 (
    .in0(x0__zero_q), .in1(x1__ra_q), .in2(x2__sp_q), .in5(x5__t0_q), .in6(x6__t1_q), .in7(x7__t2_q),
    .in8(x8__s0_q), .in9(x9__s1_q), .in10(x10__a0_q), .out(Read_Data_2), .sel(Read_Register_2__rs2));  // open: in3, in4, in11, in12, in13, in14, in15, in16, in17, in18, in19, in20, in21, in22, in23, in24, in25, in26, in27, in28, in29, in30, in31, en
endmodule

module ALU (
  input  [31:0] A,
  input  [31:0] B,
  input  [3:0] ALUSel,
  output Zero,
  output [31:0] Result,
  output Overflow
);

  wire adder_1_cout, adder_2_cout, adder_4_cout, and_1_out, comparator_1_lt, comparator_2_lt;
  wire [30:0] shifter_4_out, shifter_5_out;
  wire [31:0] _0_out, _1_out, _2_out, _3_out, _4_out, _5_out, _6_out, _7_out, _8_out, _9_out, _10_out,
       _11_out, _12_out, _13_out, _14_out, _15_out, adder_1_out, adder_2_out, adder_3_out, adder_5_out,
       adder_6_out, adder_7_out, adder_8_out, and_2_out, and_3_out, and_4_out, and_5_out, bit_extender_1_out,
       bit_extender_2_out, bit_extender_3_out, bit_extender_4_out, bit_extender_5_out, bit_extender_6_out,
       bit_extender_7_out, bit_extender_8_out, bit_extender_9_out, bit_extender_10_out, bit_extender_11_out,
       bit_extender_12_out, bit_extender_13_out, bit_extender_14_out, bit_extender_15_out,
       bit_extender_16_out, bit_extender_17_out, bit_extender_18_out, bit_extender_19_out, multiplier_1_cout,
       multiplier_1_out, multiplier_2_cout, multiplier_2_out, not_1_out, not_2_out, not_3_out, not_4_out,
       or_1_out, shifter_1_out, shifter_2_out, shifter_3_out, shifter_6_out, shifter_7_out, subtractor_1_out,
       xor_1_out;
  wire [31:1] and_6_out;

  assign bit_extender_1_out = {{31{1'b0}}, A[0]};  // Bit_Extender bit_extender_1
  assign bit_extender_2_out = {{31{1'b0}}, B[0]};  // Bit_Extender bit_extender_2
  Shifter #(.width(32)) shifter_1 (.in(bit_extender_1_out), .\dist ({5{1'b1}}), .out(shifter_1_out));
  Shifter #(.width(32)) shifter_2 (.in(bit_extender_2_out), .\dist ({5{1'b1}}), .out(shifter_2_out));
  assign bit_extender_3_out = {{1{1'b0}}, A[30:0]};  // Bit_Extender bit_extender_3
  Adder #(.width(32)) adder_1 (
    .a(shifter_1_out), .b(shifter_2_out), .out(adder_1_out), .cout(adder_1_cout));  // open: cin
  assign bit_extender_4_out = {{31{1'b0}}, adder_1_cout};  // Bit_Extender bit_extender_4
  assign bit_extender_5_out = {{31{1'b0}}, 1'b0};  // Bit_Extender bit_extender_5
  assign bit_extender_6_out = {{1{1'b0}}, B[30:0]};  // Bit_Extender bit_extender_6
  Adder #(.width(32)) adder_2 (.a(A), .b(B), .out(adder_2_out), .cout(adder_2_cout));  // open: cin
  and and_1 (and_1_out, A[31], B[31]);
  assign bit_extender_7_out = {{31{A[31]}}, A[31]};  // Bit_Extender bit_extender_7
  assign bit_extender_8_out = {{31{B[31]}}, B[31]};  // Bit_Extender bit_extender_8
  Adder #(.width(32)) adder_3 (.a(adder_5_out), .b(bit_extender_4_out), .out(adder_3_out));  // open: cin, cout
  Shifter #(.width(32), .shift("ar")) shifter_3 (.in(A), .\dist (B[4:0]), .out(shifter_3_out));
  assign bit_extender_9_out = {{31{adder_2_cout}}, adder_2_cout};  // Bit_Extender bit_extender_9
  assign bit_extender_10_out = {{31{and_1_out}}, and_1_out};  // Bit_Extender bit_extender_10
  Shifter #(.width(31), .shift("lr")) shifter_4 (.in(B[30:0]), .\dist (5'b00001), .out(shifter_4_out));
  Shifter #(.width(31), .shift("lr")) shifter_5 (.in(A[30:0]), .\dist (5'b00001), .out(shifter_5_out));
  Multiplier #(.width(32)) multiplier_1 (
    .a(bit_extender_3_out), .b(bit_extender_6_out), .out(multiplier_1_out), .cout(multiplier_1_cout));  // open: cin
  assign and_2_out = A & B;  // AND_Gate and_2, 32 bits wide
  Shifter #(.width(32), .shift("lr")) shifter_6 (.in(A), .\dist (B[4:0]), .out(shifter_6_out));
  assign bit_extender_11_out = {{31{1'b0}}, comparator_1_lt};  // Bit_Extender bit_extender_11
  Comparator #(.width(32), .mode("unsigned")) comparator_1 (.a(A), .b(B), .lt(comparator_1_lt));  // open: gt, eq
  assign bit_extender_12_out = {{31{1'b0}}, comparator_2_lt};  // Bit_Extender bit_extender_12
  Comparator #(.width(32)) comparator_2 (.a(A), .b(B), .lt(comparator_2_lt));  // open: gt, eq
  Adder #(.width(32)) adder_4 (.a(multiplier_1_out), .b(adder_1_out), .cout(adder_4_cout));  // open: out, cin
  Subtractor #(.width(32)) subtractor_1 (.a(A), .b(B), .out(subtractor_1_out));  // open: bin, bout
  Multiplier #(.width(32)) multiplier_2 (.a(B), .b(A), .out(multiplier_2_out), .cout(multiplier_2_cout));  // open: cin
  assign or_1_out = A | B;  // OR_Gate or_1, 32 bits wide
  assign xor_1_out = A ^ B;  // XOR_Gate xor_1, 32 bits wide
  Shifter #(.width(32)) shifter_7 (.in(A), .\dist (B[4:0]), .out(shifter_7_out));
  assign bit_extender_13_out = {{31{1'b0}}, adder_4_cout};  // Bit_Extender bit_extender_13
  Adder #(.width(32)) adder_5 (.a(adder_6_out), .b(bit_extender_13_out), .out(adder_5_out));  // open: cin, cout
  assign not_1_out = ~bit_extender_14_out;  // NOT_Gate not_1, 32 bits wide
  assign bit_extender_14_out = {{31{ALUSel[3]}}, ALUSel[3]};  // Bit_Extender bit_extender_14
  assign not_2_out = ~bit_extender_15_out;  // NOT_Gate not_2, 32 bits wide
  assign bit_extender_15_out = {{31{ALUSel[2]}}, ALUSel[2]};  // Bit_Extender bit_extender_15
  assign not_3_out = ~bit_extender_16_out;  // NOT_Gate not_3, 32 bits wide
  assign bit_extender_16_out = {{31{ALUSel[1]}}, ALUSel[1]};  // Bit_Extender bit_extender_16
  assign bit_extender_17_out = {{1{1'b0}}, shifter_4_out};  // Bit_Extender bit_extender_17
  assign bit_extender_18_out = {{1{1'b0}}, shifter_5_out};  // Bit_Extender bit_extender_18
  Adder #(.width(32)) adder_6 (.a(adder_8_out), .b(multiplier_1_cout), .out(adder_6_out));  // open: cin, cout
  assign not_4_out = ~bit_extender_19_out;  // NOT_Gate not_4, 32 bits wide
  assign bit_extender_19_out = {{31{ALUSel[0]}}, ALUSel[0]};  // Bit_Extender bit_extender_19
  assign and_3_out = bit_extender_7_out & bit_extender_17_out;  // AND_Gate and_3, 32 bits wide
  assign and_4_out = bit_extender_18_out & bit_extender_8_out;  // AND_Gate and_4, 32 bits wide
  assign and_5_out = bit_extender_10_out & 32'h80000000;  // AND_Gate and_5, 32 bits wide
  Adder #(.width(32)) adder_7 (.a(and_3_out), .b(and_4_out), .out(adder_7_out));  // open: cin, cout
  assign _15_out = B & bit_extender_14_out & bit_extender_15_out & bit_extender_16_out & bit_extender_19_out;  // AND_Gate _15, 32 bits wide
  assign _14_out = bit_extender_5_out & bit_extender_14_out & bit_extender_15_out & bit_extender_16_out & not_4_out;  // AND_Gate _14, 32 bits wide
  assign _13_out = bit_extender_14_out & bit_extender_15_out & not_3_out & bit_extender_19_out & shifter_3_out;  // AND_Gate _13, 32 bits wide
  assign _12_out = bit_extender_14_out & bit_extender_15_out & not_3_out & not_4_out & subtractor_1_out;  // AND_Gate _12, 32 bits wide
  assign _11_out = bit_extender_14_out & not_2_out & bit_extender_16_out & bit_extender_19_out & adder_3_out;  // AND_Gate _11, 32 bits wide
  assign _10_out = bit_extender_14_out & not_2_out & bit_extender_16_out & not_4_out & bit_extender_5_out;  // AND_Gate _10, 32 bits wide
  assign _9_out = bit_extender_14_out & not_2_out & not_3_out & bit_extender_19_out & multiplier_2_cout;  // AND_Gate _9, 32 bits wide
  assign _8_out = bit_extender_14_out & not_2_out & not_3_out & not_4_out & multiplier_2_out;  // AND_Gate _8, 32 bits wide
  assign _7_out = not_1_out & bit_extender_15_out & bit_extender_16_out & bit_extender_19_out & and_2_out;  // AND_Gate _7, 32 bits wide
  assign _6_out = not_1_out & bit_extender_15_out & bit_extender_16_out & not_4_out & or_1_out;  // AND_Gate _6, 32 bits wide
  assign _5_out = not_1_out & bit_extender_15_out & not_3_out & bit_extender_19_out & shifter_6_out;  // AND_Gate _5, 32 bits wide
  assign _4_out = not_1_out & bit_extender_15_out & not_3_out & not_4_out & xor_1_out;  // AND_Gate _4, 32 bits wide
  assign _3_out = not_1_out & not_2_out & bit_extender_16_out & bit_extender_19_out & bit_extender_11_out;  // AND_Gate _3, 32 bits wide
  assign _2_out = not_1_out & not_2_out & bit_extender_16_out & not_4_out & bit_extender_12_out;  // AND_Gate _2, 32 bits wide
  assign _1_out = not_1_out & not_2_out & not_3_out & bit_extender_19_out & shifter_7_out;  // AND_Gate _1, 32 bits wide
  assign _0_out = not_4_out & not_3_out & not_2_out & not_1_out & adder_2_out;  // AND_Gate _0, 32 bits wide
  assign {and_6_out, Overflow} = not_4_out & not_3_out & not_2_out & not_1_out & bit_extender_9_out;  // AND_Gate and_6, 32 bits wide
  Adder #(.width(32)) adder_8 (.a(and_5_out), .b(adder_7_out), .out(adder_8_out));  // open: cin, cout
  assign Result = _15_out | _14_out | _13_out | _12_out | _11_out | _10_out | _9_out | _8_out | _7_out | _6_out | _5_out | _4_out | _3_out | _2_out | _1_out | _0_out;  // OR_Gate or_2, 32 bits wide
  Comparator #(.width(32)) comparator_3 (.a(bit_extender_5_out), .b(Result), .eq(Zero));  // open: gt, lt
endmodule

// DATA MEM
module data_mem (
  input  [8:0] A,
  input  CLK,
  input  WE,
  input  [31:0] WD,
  output [31:0] RD
);

  wire not_1_out;

  RAM #(.addrWidth(9), .dataWidth(32)) ram_1 (.addr(A), .data(RD), .clk(CLK), .ld(not_1_out));  // open: sel, clr
  not not_1 (not_1_out, WE);
  assign RD = WE ? WD : 32'bz;  // Controlled_Buffer controlled_buffer_1
endmodule

module Control_unit (
  input  op6,
  input  op5,
  input  op4,
  input  op3,
  input  op2,
  input  op1,
  input  op0,
  output RegWrite,
  output [1:0] ImmGen,
  output ALUSrc,
  output MemWrite,
  output MemToReg,
  output Branch,
  output ALUOp1,
  output ALUOp0
);

  wire and_2_out, not_1_out, not_2_out, not_3_out, not_4_out, not_5_out, not_6_out, not_8_out;

  not not_1 (not_1_out, op5);
  not not_2 (not_2_out, op6);
  not not_3 (not_3_out, op6);
  not not_4 (not_4_out, op4);
  not not_5 (not_5_out, op6);
  not not_6 (not_6_out, op4);
  not not_7 (MemToReg, op4);
  or or_1 (RegWrite, not_1_out, op4);
  and and_1 (ImmGen[0], not_2_out, op5);
  and and_2 (and_2_out, not_3_out, not_4_out);
  not not_8 (not_8_out, op5);
  and and_3 (MemWrite, not_5_out, op5, not_6_out);
  or or_2 (ALUSrc, and_2_out, not_8_out);

  assign ALUOp0 = op6;
  assign ALUOp1 = op4;
  assign Branch = op6;
  assign ImmGen[1] = op6;
endmodule

module ALUCntrl (
  input  ALUOp1,
  input  ALUOp0,
  input  Func14,
  input  Func13,
  input  Func12,
  input  Op5,
  input  Func30,
  output ALUControl3,
  output ALUControl2,
  output ALUControl1,
  output ALUControl0
);

  wire and_3_out, and_4_out, and_5_out, not_1_out, not_2_out, not_3_out, not_4_out, not_5_out;

  not not_1 (not_1_out, Func14);
  not not_2 (not_2_out, Func13);
  not not_3 (not_3_out, Func12);
  not not_4 (not_4_out, Func13);
  not not_5 (not_5_out, Func12);
  and and_1 (ALUControl1, ALUOp1, Func13);
  and and_2 (ALUControl0, ALUOp1, Func12);
  and and_3 (and_3_out, ALUOp1, not_1_out, not_2_out, not_3_out, Op5, Func30);
  and and_4 (and_4_out, ALUOp1, not_4_out, not_5_out, Op5, Func30);
  and and_5 (and_5_out, ALUOp1, Func14);
  or or_1 (ALUControl3, ALUOp0, and_3_out);
  or or_2 (ALUControl2, ALUOp0, and_4_out, and_5_out);
endmodule

// MAIN COntrol Unit
module CONTROL_UNIT (
  input  [6:0] OPCode,
  input  [3:0] Func,
  output RegWrite,
  output [1:0] ImmGen,
  output ALUSrc,
  output Branch,
  output MemWrite,
  output MemToReg,
  output [3:0] ALUControl
);

  wire control_unit_1_aluop0, control_unit_1_aluop1;

  Control_unit control_unit_1 (
    .op6(OPCode[6]), .RegWrite(RegWrite), .op5(OPCode[5]), .op4(OPCode[4]), .ALUSrc(ALUSrc), .op3(OPCode[3]),
    .op2(OPCode[2]), .MemWrite(MemWrite), .op1(OPCode[1]), .MemToReg(MemToReg), .op0(OPCode[0]),
    .Branch(Branch), .ALUOp1(control_unit_1_aluop1), .ALUOp0(control_unit_1_aluop0), .ImmGen(ImmGen));
  ALUCntrl alucntrl_1 (
    .ALUOp1(control_unit_1_aluop1), .ALUOp0(control_unit_1_aluop0), .Func14(Func[2]), .Func13(Func[1]),
    .Func12(Func[0]), .Op5(OPCode[5]), .Func30(Func[3]), .ALUControl3(ALUControl[3]),
    .ALUControl2(ALUControl[2]), .ALUControl1(ALUControl[1]), .ALUControl0(ALUControl[0]));
endmodule

// Imm
module ImmGen (
  input  [1:0] ImmSrc,
  input  [31:0] Inst,
  output [31:0] out_3
);

  wire [11:0] multiplexer_1_out;

  Multiplexer #(.select(2), .width(12), .enable("false")) multiplexer_1 (
    .in0(Inst[31:20]), .in1({Inst[31:25], Inst[11:7]}), .in2({Inst[31], Inst[7], Inst[30:25], Inst[11:8]}),
    .out(multiplexer_1_out), .sel(ImmSrc));  // open: in3
  assign out_3 = {{20{1'b0}}, multiplexer_1_out};  // Bit_Extender bit_extender_1
endmodule
